// Logisim project ALU.circ as structural Verilog
module ALU (
  input  [1:0] in_1,
  input  [31:0] RS_DATA,
  input  [31:0] RT_DATA,
  input  [4:0] in_4,
  input  [4:0] I,
  input  [7:0] B,
  output [31:0] output_of_ALU
);

  wire comparator_1_eq, comparator_1_gt, comparator_1_lt, comparator_2_eq, comparator_2_lt, comparator_3_eq,
       comparator_3_lt, not_1_out;
  wire [31:0] Add, Addi, And, Andi, Beq, Beqz, Bgez, Bgtz, bit_extender_1_out, bit_extender_2_out,
       bit_extender_4_out, Blez, Bltz, Bnq, Bnqz, Eqv, Eqvi, Jr_Jalr, Lw_Sw, multiplexer_1_out,
       multiplexer_2_out, Or, Ori, Ror, Seq, Seqi, Set, shifter_1_out, shifter_5_out, Sll, Slt, Slti, Srl,
       Sset, Sub, Xnor, Xor, Xori;

  assign bit_extender_1_out = {{27{I[4]}}, I};  // Bit_Extender bit_extender_1
  assign bit_extender_2_out = {{27{1'b0}}, I};  // Bit_Extender bit_extender_2
  Comparator #(.width(32)) comparator_1 (
    .a(RT_DATA), .b({32{1'b0}}), .gt(comparator_1_gt), .eq(comparator_1_eq), .lt(comparator_1_lt));
  assign Set = {{24{B[7]}}, B};  // Bit_Extender bit_extender_3
  Shifter #(.width(32)) shifter_1 (.in(RT_DATA), .\dist (5'b01000), .out(shifter_1_out));
  assign bit_extender_4_out = {{24{1'b0}}, B};  // Bit_Extender bit_extender_4
  Comparator #(.width(32)) comparator_2 (
    .a(RS_DATA), .b(RT_DATA), .eq(comparator_2_eq), .lt(comparator_2_lt));  // open: gt
  Adder #(.width(32)) adder_1 (.a(RS_DATA), .b(bit_extender_1_out), .out(Addi));  // open: cin, cout
  Comparator #(.width(32)) comparator_3 (
    .a(RS_DATA), .b(bit_extender_1_out), .eq(comparator_3_eq), .lt(comparator_3_lt));  // open: gt
  Shifter #(.width(32)) shifter_2 (.in(RS_DATA), .\dist (I), .out(Sll));
  Shifter #(.width(32), .shift("lr")) shifter_3 (.in(RS_DATA), .\dist (I), .out(Srl));
  Shifter #(.width(32), .shift("rr")) shifter_4 (.in(RS_DATA), .\dist (I), .out(Ror));
  Adder #(.width(32)) adder_2 (.a(bit_extender_1_out), .b(RS_DATA), .out(Lw_Sw));  // open: cin, cout
  Shifter #(.width(32)) shifter_5 (.in(Set), .\dist (5'b00001), .out(shifter_5_out));
  assign Sset = shifter_1_out | bit_extender_4_out;  // OR_Gate or_1, 32 bits wide
  assign And = RS_DATA & RT_DATA;  // AND_Gate and_1, 32 bits wide
  assign Or = RS_DATA | RT_DATA;  // OR_Gate or_2, 32 bits wide
  assign Xor = RS_DATA ^ RT_DATA;  // XOR_Gate xor_1, 32 bits wide
  assign Eqv = ~(RS_DATA ^ RT_DATA);  // XNOR_Gate xnor_1, 32 bits wide
  Adder #(.width(32)) adder_3 (.a(RS_DATA), .b(RT_DATA), .out(Add));  // open: cin, cout
  assign Seq = {{31{1'b0}}, comparator_2_eq};  // Bit_Extender bit_extender_5
  assign Slt = {{31{1'b0}}, comparator_2_lt};  // Bit_Extender bit_extender_6
  not not_1 (not_1_out, comparator_2_eq);
  assign Seqi = {{31{1'b0}}, comparator_3_eq};  // Bit_Extender bit_extender_7
  assign Slti = {{31{1'b0}}, comparator_3_lt};  // Bit_Extender bit_extender_8
  assign Andi = RS_DATA & bit_extender_2_out;  // AND_Gate and_2, 32 bits wide
  assign Ori = RS_DATA | bit_extender_2_out;  // OR_Gate or_3, 32 bits wide
  assign Xori = RS_DATA ^ bit_extender_2_out;  // XOR_Gate xor_2, 32 bits wide
  assign Eqvi = ~(RS_DATA ^ bit_extender_2_out);  // XNOR_Gate xnor_2, 32 bits wide
  assign Bgtz = {{31{1'b0}}, comparator_1_gt};  // Bit_Extender bit_extender_9
  assign Beqz = {{31{1'b0}}, comparator_1_eq};  // Bit_Extender bit_extender_10
  assign Bnqz = ~Beqz;  // NOT_Gate not_2, 32 bits wide
  assign Bltz = {{31{1'b0}}, comparator_1_lt};  // Bit_Extender bit_extender_11
  Adder #(.width(32)) adder_4 (.a(shifter_5_out), .b(RT_DATA), .out(Jr_Jalr));  // open: cin, cout
  Subtractor #(.width(32)) subtractor_1 (.a(RS_DATA), .b(RT_DATA), .out(Sub));  // open: bin, bout
  assign Beq = {{31{1'b0}}, comparator_2_eq};  // Bit_Extender bit_extender_12
  assign Bnq = {{31{1'b0}}, not_1_out};  // Bit_Extender bit_extender_13
  assign Bgez = Bgtz | Beqz;  // OR_Gate or_4, 32 bits wide
  assign Blez = Beqz | Bltz;  // OR_Gate or_5, 32 bits wide
  Multiplexer #(.select(2), .width(32)) multiplexer_1 (
    .in0(And), .in1(Or), .in2(Eqv), .in3(Xnor), .out(multiplexer_1_out), .sel(in_1));  // open: en
  Multiplexer #(.select(2), .width(32)) multiplexer_2 (
    .in0(Add), .in1(Sub), .in2(Slt), .in3(Seq), .out(multiplexer_2_out), .sel(in_1));  // open: en
  Multiplexer #(.select(5), .width(32)) multiplexer_3 (
    .in0(multiplexer_1_out), .in1(multiplexer_2_out), .in2({32{1'b0}}), .in3({32{1'b0}}), .in4(Andi),
    .in5(Ori), .in6(Xori), .in7(Eqvi), .in8(Addi), .in9(Slti), .in10(Seqi), .in11(Sll), .in12(Srl),
    .in13(Ror), .in14(Beq), .in15(Bnq), .in16(Lw_Sw), .in17(Lw_Sw), .in18({32{1'b0}}), .in19({32{1'b0}}),
    .in20(Beqz), .in21(Bnqz), .in22(Bltz), .in23(Bgez), .in24(Bgtz), .in25(Blez), .in26(Jr_Jalr),
    .in27(Jr_Jalr), .in28(Set), .in29(Sset), .in30({32{1'b0}}), .in31({32{1'b0}}), .out(output_of_ALU),
    .sel(in_4));  // open: en
endmodule
