// Logisim project Project.circ as structural Verilog: 42 circuits, main circuit main
module main (
  input  in_1,
  input  in_2,
  input  in_3,
  input  Clear,
  input  Clear_2,
  output over_flow_flag
);

  wire and_1_out, b_1, branch, clock_1_out, j_src, M_read, M_write, reg_src, REG_WRITE;
  wire [1:0] add_sub, Memtoreg, pcnext, reg_des;
  wire [2:0] b_all, multiplexer_1_out, multiplexer_2_out, multiplexer_3_out;
  wire [4:0] ALU_OP, OP_CODE;
  wire [7:0] _8_imm;
  wire [10:8] ram_1_data;
  wire [19:0] _0_10_J_type, adder_1_out, adder_3_out, bit_extender_1_out, bit_extender_2_out, Jr_Jalr,
       multiplexer_4_out, next_pc, PC_q, shifter_1_out;
  wire [31:0] alu_out, bit_extender_3_out, data_in, multiplexer_6_out, ram_2_data, rs_data;

  Clock clock_1 (.out(clock_1_out));
  Register #(.width(20)) PC (.D(next_pc), .en(in_2), .Q(PC_q), .clk(clock_1_out), .clr(Clear_2));
  Adder #(.width(20)) adder_1 (.a(PC_q), .b(20'h1), .out(adder_1_out), .cin(1'b0));  // open: cout
  Adder #(.width(20)) adder_2 (.a(shifter_1_out), .b(PC_q), .out(_0_10_J_type));  // open: cin, cout
  Shifter #(.width(20)) shifter_1 (.in(bit_extender_1_out), .\dist (5'b00001), .out(shifter_1_out));
  assign bit_extender_1_out = {{9{ram_1_data[10]}}, {ram_1_data, _8_imm}};  // Bit_Extender bit_extender_1
  RAM #(.addrWidth(20), .dataWidth(16)) ram_1 (
    .addr(PC_q), .data({OP_CODE, ram_1_data, _8_imm}), .sel(in_3), .clk(clock_1_out), .ld(1'b1), .clr(Clear));
  assign bit_extender_2_out = {{15{_8_imm[4]}}, _8_imm[4:0]};  // Bit_Extender bit_extender_2
  Multiplexer #(.width(3), .enable("false")) multiplexer_1 (
    .in0(_8_imm[4:2]), .in1(ram_1_data), .out(multiplexer_1_out), .sel(reg_src));
  Adder #(.width(20)) adder_3 (.a(adder_1_out), .b(bit_extender_2_out), .out(adder_3_out));  // open: cin, cout
  Multiplexer #(.select(2), .width(3), .enable("false")) multiplexer_2 (
    .in0(_8_imm[4:2]), .in1(ram_1_data), .out(multiplexer_2_out), .sel(reg_des));  // open: in2, in3
  assign bit_extender_3_out = {{12{adder_1_out[19]}}, adder_1_out};  // Bit_Extender bit_extender_3
  Multiplexer #(.width(3), .enable("false")) multiplexer_3 (
    .in0(multiplexer_2_out), .in1(3'b111), .out(multiplexer_3_out), .sel(j_src));
  Reg_File Reg_File (
    .Ra(_8_imm[7:5]), .Rb(multiplexer_1_out), .RW(multiplexer_3_out), .BUS_W(multiplexer_6_out),
    .bus_a(rs_data), .bus_B(data_in), .REG_WRITE(REG_WRITE), .clock(clock_1_out));
  and and_1 (and_1_out, branch, b_1);
  Multiplexer #(.width(20), .enable("false")) multiplexer_4 (
    .in0(adder_1_out), .in1(adder_3_out), .out(multiplexer_4_out), .sel(and_1_out));
  Multiplexer #(.select(2), .width(20), .enable("false")) multiplexer_5 (
    .in0(adder_1_out), .in1(_0_10_J_type), .in2(multiplexer_4_out), .in3(Jr_Jalr), .out(next_pc), .sel(pcnext));
  ALU ALU (
    .RS_DATA(rs_data), .in_2(_8_imm[1:0]), .RT_DATA(data_in), .I(_8_imm[4:0]), .B(_8_imm),
    .output_of_ALU(alu_out), .in_5(ALU_OP), .add_sub(add_sub), .over_flow_flag(over_flow_flag),
    .b_all(b_all), .out_11(b_1));
  Control_Unit control_unit_1 (
    .out_3(j_src), .out_4(b_all), .out_5(branch), .out_6(pcnext), .out_7(Memtoreg), .out_8(M_read),
    .out_9(M_write), .out_10(reg_src), .out_11(REG_WRITE), .out_12(reg_des), .out_13(add_sub),
    .out_14(ALU_OP), .in_2(OP_CODE), .in_1(_8_imm[1:0]));
  RAM #(.addrWidth(23), .dataWidth(32), .bus("separate")) ram_2 (
    .addr(alu_out[22:0]), .din(data_in), .data(ram_2_data), .str(M_write), .clk(clock_1_out), .ld(M_read));  // open: sel, clr
  Multiplexer #(.select(2), .width(32), .enable("false")) multiplexer_6 (
    .in0(alu_out), .in1(ram_2_data), .in2(bit_extender_3_out), .out(multiplexer_6_out), .sel(Memtoreg));  // open: in3

  // Other names for the same wires on the sheet: F[1:0] = _8_imm[1:0]; rt_data[31:0] = data_in

  // Notes on the sheet:
  //   reg-dest
  //   Rs
  //   Rt
  //   Rd
  //   I-TYPE
  //   BUS A
  //   BUS B
  //   mem-reg
endmodule

module ALU (
  input  [31:0] RS_DATA,
  input  [1:0] in_2,
  input  [31:0] RT_DATA,
  input  [1:0] add_sub,
  input  [4:0] in_5,
  input  [4:0] I,
  input  [2:0] b_all,
  input  [7:0] B,
  output over_flow_flag,
  output [31:0] output_of_ALU,
  output out_11
);

  wire adder_1_cout, Beq, Beqz, Bgez, Bgtz, Blez, Bltz, Bnez, Bnq, comparator_1_lt, comparator_3_eq,
       comparator_3_lt, subtractor_1_bout;
  wire [19:0] Jr_Jalr;
  wire [31:0] Add, Addi, And, Andi, bit_extender_1_out, bit_extender_2_out, bit_extender_4_out, Eqv, Eqvi,
       Lw_Sw, multiplexer_3_out, multiplexer_4_out, Or, Ori, Ror, Seq, Seqi, Set, shifter_1_out,
       shifter_5_out, Sll, Slt, Slti, Srl, Sset, Sub, undriven, Xnor, Xor, Xori;
  wire [31:20] adder_4_out;

  assign And = RS_DATA & RT_DATA;  // AND_Gate and_1, 32 bits wide
  assign Or = RS_DATA | RT_DATA;  // OR_Gate or_1, 32 bits wide
  assign Xor = RS_DATA ^ RT_DATA;  // XOR_Gate xor_1, 32 bits wide
  assign Eqv = ~(RS_DATA ^ RT_DATA);  // XNOR_Gate xnor_1, 32 bits wide
  Adder #(.width(32)) adder_1 (.a(RS_DATA), .b(RT_DATA), .out(Add), .cout(adder_1_cout));  // open: cin
  Subtractor #(.width(32)) subtractor_1 (.a(RS_DATA), .b(RT_DATA), .out(Sub), .bout(subtractor_1_bout));  // open: bin
  Comparator #(.width(32)) comparator_1 (.a(RS_DATA), .b(RT_DATA), .eq(Beq), .lt(comparator_1_lt));  // open: gt
  assign bit_extender_1_out = {{27{I[4]}}, I};  // Bit_Extender bit_extender_1
  assign bit_extender_2_out = {{27{1'b0}}, I};  // Bit_Extender bit_extender_2
  Comparator #(.width(32)) comparator_2 (.a(RT_DATA), .b({32{1'b0}}), .gt(Bgtz), .eq(Beqz), .lt(Bltz));
  assign Set = {{24{B[7]}}, B};  // Bit_Extender bit_extender_3
  Shifter #(.width(32)) shifter_1 (.in(RT_DATA), .\dist (5'b01000), .out(shifter_1_out));
  assign bit_extender_4_out = {{24{1'b0}}, B};  // Bit_Extender bit_extender_4
  assign Seq = {{31{1'b0}}, Beq};  // Bit_Extender bit_extender_5
  assign Slt = {{31{1'b0}}, comparator_1_lt};  // Bit_Extender bit_extender_6
  not not_1 (Bnq, Beq);
  Adder #(.width(32)) adder_2 (.a(RS_DATA), .b(bit_extender_1_out), .out(Addi));  // open: cin, cout
  Comparator #(.width(32)) comparator_3 (
    .a(RS_DATA), .b(bit_extender_1_out), .eq(comparator_3_eq), .lt(comparator_3_lt));  // open: gt
  Shifter #(.width(32)) shifter_2 (.in(RS_DATA), .\dist (I), .out(Sll));
  Shifter #(.width(32), .shift("lr")) shifter_3 (.in(RS_DATA), .\dist (I), .out(Srl));
  Shifter #(.width(32), .shift("rr")) shifter_4 (.in(RS_DATA), .\dist (I), .out(Ror));
  Adder #(.width(32)) adder_3 (.a(bit_extender_1_out), .b(RS_DATA), .out(Lw_Sw));  // open: cin, cout
  not not_2 (Bnez, Beqz);
  Shifter #(.width(32)) shifter_5 (.in(Set), .\dist (5'b00001), .out(shifter_5_out));
  Adder #(.width(32)) adder_4 (.a(shifter_5_out), .b(RT_DATA), .out({adder_4_out, Jr_Jalr}));  // open: cin, cout
  assign Sset = shifter_1_out | bit_extender_4_out;  // OR_Gate or_2, 32 bits wide
  assign Seqi = {{31{1'b0}}, comparator_3_eq};  // Bit_Extender bit_extender_7
  assign Slti = {{31{1'b0}}, comparator_3_lt};  // Bit_Extender bit_extender_8
  assign Andi = RS_DATA & bit_extender_2_out;  // AND_Gate and_2, 32 bits wide
  assign Ori = RS_DATA | bit_extender_2_out;  // OR_Gate or_3, 32 bits wide
  assign Xori = RS_DATA ^ bit_extender_2_out;  // XOR_Gate xor_2, 32 bits wide
  assign Eqvi = ~(RS_DATA ^ bit_extender_2_out);  // XNOR_Gate xnor_2, 32 bits wide
  or or_4 (Bgez, Bgtz, Beqz);
  or or_5 (Blez, Beqz, Bltz);
  Multiplexer #(.select(2), .enable("false")) multiplexer_1 (
    .in0(adder_1_cout), .in1(subtractor_1_bout), .in2(1'b0), .in3(1'b0), .out(over_flow_flag), .sel(add_sub));
  Multiplexer #(.select(3), .enable("false")) multiplexer_2 (
    .in0(Beq), .in1(Bnq), .in2(Beqz), .in3(Bnez), .in4(Bltz), .in5(Bgez), .in6(Bgtz), .in7(Blez),
    .out(out_11), .sel(b_all));
  Multiplexer #(.select(2), .width(32), .enable("false")) multiplexer_3 (
    .in0(And), .in1(Or), .in2(Xnor), .in3(Eqv), .out(multiplexer_3_out), .sel(in_2));
  Multiplexer #(.select(2), .width(32), .enable("false")) multiplexer_4 (
    .in0(Add), .in1(Sub), .in2(Slt), .in3(Seq), .out(multiplexer_4_out), .sel(in_2));
  Multiplexer #(.select(5), .width(32), .enable("false")) multiplexer_5 (
    .in0(multiplexer_3_out), .in1(multiplexer_4_out), .in2({32{1'b0}}), .in3({32{1'b0}}), .in4(Andi),
    .in5(Ori), .in6(Xori), .in7(Eqvi), .in8(Addi), .in9(Slti), .in10(Seqi), .in11(Sll), .in12(Srl),
    .in13(Ror), .in16(Lw_Sw), .in17(Lw_Sw), .in18({32{1'b0}}), .in19({32{1'b0}}), .in26(undriven),
    .in27(undriven), .in28(Set), .in29(Sset), .in30({32{1'b0}}), .in31({32{1'b0}}), .out(output_of_ALU),
    .sel(in_5));  // open: in14, in15, in20, in21, in22, in23, in24, in25
endmodule

module Reg_File (
  input  [2:0] Ra,
  input  [2:0] Rb,
  input  [2:0] RW,
  input  REG_WRITE,
  input  clock,
  input  [31:0] BUS_W,
  output [31:0] bus_a,
  output [31:0] bus_B
);

  wire and_1_out, and_2_out, and_3_out, and_4_out, and_5_out, and_6_out, and_7_out, and_8_out,
       decoder_1_out0, decoder_1_out1, decoder_1_out2, decoder_1_out3, decoder_1_out4, decoder_1_out5,
       decoder_1_out6, decoder_1_out7, decoder_2_out0, decoder_2_out1, decoder_2_out2, decoder_2_out3,
       decoder_2_out4, decoder_2_out5, decoder_2_out6, decoder_2_out7, decoder_3_out0, decoder_3_out1,
       decoder_3_out2, decoder_3_out3, decoder_3_out4, decoder_3_out5, decoder_3_out6, decoder_3_out7;
  wire [31:0] register_1_q, register_2_q, register_3_q, register_4_q, register_5_q, register_6_q,
       register_7_q, register_8_q;

  Decoder #(.select(3), .enable("false")) decoder_1 (
    .out0(decoder_1_out0), .out1(decoder_1_out1), .out2(decoder_1_out2), .out3(decoder_1_out3),
    .out4(decoder_1_out4), .out5(decoder_1_out5), .out6(decoder_1_out6), .out7(decoder_1_out7), .sel(RW));
  and and_1 (and_1_out, decoder_1_out0, REG_WRITE);
  and and_2 (and_2_out, decoder_1_out1, REG_WRITE);
  and and_3 (and_3_out, decoder_1_out2, REG_WRITE);
  and and_4 (and_4_out, decoder_1_out3, REG_WRITE);
  and and_5 (and_5_out, decoder_1_out4, REG_WRITE);
  and and_6 (and_6_out, decoder_1_out5, REG_WRITE);
  and and_7 (and_7_out, decoder_1_out6, REG_WRITE);
  and and_8 (and_8_out, decoder_1_out7, REG_WRITE);
  Register #(.width(32)) register_1 (.D(BUS_W), .en(and_1_out), .Q(register_1_q), .clk(clock));  // open: clr
  Register #(.width(32)) register_2 (.D(BUS_W), .en(and_2_out), .Q(register_2_q), .clk(clock));  // open: clr
  Register #(.width(32)) register_3 (.D(BUS_W), .en(and_3_out), .Q(register_3_q), .clk(clock));  // open: clr
  Register #(.width(32)) register_4 (.D(BUS_W), .en(and_4_out), .Q(register_4_q), .clk(clock));  // open: clr
  Register #(.width(32)) register_5 (.D(BUS_W), .en(and_5_out), .Q(register_5_q), .clk(clock));  // open: clr
  Register #(.width(32)) register_6 (.D(BUS_W), .en(and_6_out), .Q(register_6_q), .clk(clock));  // open: clr
  Register #(.width(32)) register_7 (.D(BUS_W), .en(and_7_out), .Q(register_7_q), .clk(clock));  // open: clr
  Register #(.width(32)) register_8 (.D(BUS_W), .en(and_8_out), .Q(register_8_q), .clk(clock));  // open: clr
  Decoder #(.select(3), .enable("false")) decoder_2 (
    .out0(decoder_2_out0), .out1(decoder_2_out1), .out2(decoder_2_out2), .out3(decoder_2_out3),
    .out4(decoder_2_out4), .out5(decoder_2_out5), .out6(decoder_2_out6), .out7(decoder_2_out7), .sel(Ra));
  assign bus_a = decoder_2_out0 ? register_1_q : 32'bz;  // Controlled_Buffer controlled_buffer_1
  assign bus_a = decoder_2_out1 ? register_2_q : 32'bz;  // Controlled_Buffer controlled_buffer_2
  assign bus_a = decoder_2_out2 ? register_3_q : 32'bz;  // Controlled_Buffer controlled_buffer_3
  assign bus_a = decoder_2_out3 ? register_4_q : 32'bz;  // Controlled_Buffer controlled_buffer_4
  assign bus_a = decoder_2_out4 ? register_5_q : 32'bz;  // Controlled_Buffer controlled_buffer_5
  assign bus_a = decoder_2_out5 ? register_6_q : 32'bz;  // Controlled_Buffer controlled_buffer_6
  assign bus_a = decoder_2_out6 ? register_7_q : 32'bz;  // Controlled_Buffer controlled_buffer_7
  assign bus_a = decoder_2_out7 ? register_8_q : 32'bz;  // Controlled_Buffer controlled_buffer_8
  Decoder #(.select(3), .enable("false")) decoder_3 (
    .out0(decoder_3_out0), .out1(decoder_3_out1), .out2(decoder_3_out2), .out3(decoder_3_out3),
    .out4(decoder_3_out4), .out5(decoder_3_out5), .out6(decoder_3_out6), .out7(decoder_3_out7), .sel(Rb));
  assign bus_B = decoder_3_out0 ? register_1_q : 32'bz;  // Controlled_Buffer controlled_buffer_9
  assign bus_B = decoder_3_out1 ? register_2_q : 32'bz;  // Controlled_Buffer controlled_buffer_10
  assign bus_B = decoder_3_out2 ? register_3_q : 32'bz;  // Controlled_Buffer controlled_buffer_11
  assign bus_B = decoder_3_out3 ? register_4_q : 32'bz;  // Controlled_Buffer controlled_buffer_12
  assign bus_B = decoder_3_out4 ? register_5_q : 32'bz;  // Controlled_Buffer controlled_buffer_13
  assign bus_B = decoder_3_out5 ? register_6_q : 32'bz;  // Controlled_Buffer controlled_buffer_14
  assign bus_B = decoder_3_out6 ? register_7_q : 32'bz;  // Controlled_Buffer controlled_buffer_15
  assign bus_B = decoder_3_out7 ? register_8_q : 32'bz;  // Controlled_Buffer controlled_buffer_16

  // Notes on the sheet:
  //   RW: pull=down
endmodule

module Control_Unit (
  input  [1:0] in_1,
  input  [4:0] in_2,
  output out_3,
  output [2:0] out_4,
  output out_5,
  output [1:0] out_6,
  output [1:0] out_7,
  output out_8,
  output out_9,
  output out_10,
  output out_11,
  output [1:0] out_12,
  output [1:0] out_13,
  output [4:0] out_14
);

  wire [21:0] b_type_1_out_1, b_type_1_out_2, b_type_1_out_3, b_type_1_out_4, b_type_1_out_5, b_type_1_out_6,
       b_type_1_out_7, b_type_1_out_8, b_type_1_out_9, b_type_1_out_10, i_type_1_out_1, i_type_1_out_2,
       i_type_1_out_3, i_type_1_out_4, i_type_1_out_5, i_type_1_out_6, i_type_1_out_7, i_type_1_out_8,
       i_type_1_out_9, i_type_1_out_10, i_type_1_out_11, i_type_1_out_12, i_type_1_out_13, i_type_1_out_14,
       j_type_1_out_1, j_type_1_out_2, multiplexer_1_out, multiplexer_2_out, r_type_1_out_1, r_type_1_out_2,
       r_type_1_out_3, r_type_1_out_4, r_type_1_out_5, r_type_1_out_6, r_type_1_out_7, r_type_1_out_8;

  R_Type r_type_1 (
    .out_1(r_type_1_out_1), .out_2(r_type_1_out_2), .out_3(r_type_1_out_3), .out_4(r_type_1_out_4),
    .out_5(r_type_1_out_5), .out_6(r_type_1_out_6), .out_7(r_type_1_out_7), .out_8(r_type_1_out_8));
  I_Type i_type_1 (
    .out_1(i_type_1_out_1), .out_2(i_type_1_out_2), .out_3(i_type_1_out_3), .out_4(i_type_1_out_4),
    .out_5(i_type_1_out_5), .out_6(i_type_1_out_6), .out_7(i_type_1_out_7), .out_8(i_type_1_out_8),
    .out_9(i_type_1_out_9), .out_10(i_type_1_out_10), .out_11(i_type_1_out_11), .out_12(i_type_1_out_12),
    .out_13(i_type_1_out_13), .out_14(i_type_1_out_14));
  B_Type b_type_1 (
    .out_1(b_type_1_out_1), .out_2(b_type_1_out_2), .out_3(b_type_1_out_3), .out_4(b_type_1_out_4),
    .out_5(b_type_1_out_5), .out_6(b_type_1_out_6), .out_7(b_type_1_out_7), .out_8(b_type_1_out_8),
    .out_9(b_type_1_out_9), .out_10(b_type_1_out_10));
  Multiplexer #(.select(2), .width(22), .enable("false")) multiplexer_1 (
    .in0(r_type_1_out_1), .in1(r_type_1_out_2), .in2(r_type_1_out_3), .in3(r_type_1_out_4),
    .out(multiplexer_1_out), .sel(in_1));
  Multiplexer #(.select(2), .width(22), .enable("false")) multiplexer_2 (
    .in0(r_type_1_out_5), .in1(r_type_1_out_6), .in2(r_type_1_out_7), .in3(r_type_1_out_8),
    .out(multiplexer_2_out), .sel(in_1));
  J_Type j_type_1 (.out_1(j_type_1_out_1), .out_2(j_type_1_out_2));
  Multiplexer #(.select(5), .width(22), .enable("false")) multiplexer_3 (
    .in0(multiplexer_1_out), .in1(multiplexer_2_out), .in4(i_type_1_out_1), .in5(i_type_1_out_2),
    .in6(i_type_1_out_3), .in7(i_type_1_out_4), .in8(i_type_1_out_5), .in9(i_type_1_out_6),
    .in10(i_type_1_out_7), .in11(i_type_1_out_8), .in12(i_type_1_out_9), .in13(i_type_1_out_10),
    .in14(i_type_1_out_11), .in15(i_type_1_out_12), .in16(i_type_1_out_13), .in17(i_type_1_out_14),
    .in20(b_type_1_out_1), .in21(b_type_1_out_2), .in22(b_type_1_out_3), .in23(b_type_1_out_4),
    .in24(b_type_1_out_5), .in25(b_type_1_out_6), .in26(b_type_1_out_7), .in27(b_type_1_out_8),
    .in28(b_type_1_out_9), .in29(b_type_1_out_10), .in30(j_type_1_out_1), .in31(j_type_1_out_2),
    .out({out_14, out_13, out_12, out_11, out_10, out_9, out_8, out_7, out_6, out_5, out_4, out_3}),
    .sel(in_2));  // open: in2, in3, in18, in19
endmodule

module J (
  output [21:0] out_1
);


  assign {out_1[16:15], out_1[12], out_1[10:9], out_1[6:5], out_1[0]} = 8'he2;
endmodule

module jal (
  output [21:0] out_1
);


  assign {out_1[16:15], out_1[12], out_1[10:5], out_1[0]} = 10'h393;
endmodule

module R_Type (
  output [21:0] out_1,
  output [21:0] out_2,
  output [21:0] out_3,
  output [21:0] out_4,
  output [21:0] out_5,
  output [21:0] out_6,
  output [21:0] out_7,
  output [21:0] out_8
);

  \and  and_1 (.out_1(out_1));
  \or  or_1 (.out_1(out_2));
  \xor  xor_1 (.out_1(out_3));
  eqv eqv_1 (.out_1(out_4));
  add add_1 (.out_1(out_5));
  sub sub_1 (.out_1(out_6));
  slt slt_1 (.out_1(out_7));
  seq seq_1 (.out_1(out_8));
endmodule

module \and  (
  output [21:0] out_1
);


  assign out_1 = 22'h1b000;
endmodule

module \or  (
  output [21:0] out_1
);


  assign out_1 = 22'h1b000;
endmodule

module \xor  (
  output [21:0] out_1
);


  assign out_1 = 22'h1b000;
endmodule

module eqv (
  output [21:0] out_1
);


  assign out_1 = 22'h1b000;
endmodule

module add (
  output [21:0] out_1
);


  assign out_1 = 22'h23000;
endmodule

module sub (
  output [21:0] out_1
);


  assign out_1 = 22'h2b000;
endmodule

module slt (
  output [21:0] out_1
);


  assign out_1 = 22'h3b000;
endmodule

module seq (
  output [21:0] out_1
);


  assign out_1 = 22'h3b000;
endmodule

module J_Type (
  output [21:0] out_1,
  output [21:0] out_2
);

  J j_1 (.out_1(out_1));
  jal jal_1 (.out_1(out_2));
endmodule

module andi (
  output [21:0] out_1
);


  assign out_1 = 22'h9b000;
endmodule

module ori (
  output [21:0] out_1
);


  assign out_1 = 22'hbb000;
endmodule

module xori (
  output [21:0] out_1
);


  assign out_1 = 22'hdb000;
endmodule

module eqvi (
  output [21:0] out_1
);


  assign out_1 = 22'hfb000;
endmodule

module addi (
  output [21:0] out_1
);


  assign out_1 = 22'h11b000;
endmodule

module slti (
  output [21:0] out_1
);


  assign out_1 = 22'h13b000;
endmodule

module seqi (
  output [21:0] out_1
);


  assign out_1 = 22'h15b000;
endmodule

module sll (
  output [21:0] out_1
);


  assign out_1 = 22'h17b000;
endmodule

module srl (
  output [21:0] out_1
);


  assign out_1 = 22'h19b000;
endmodule

module ror (
  output [21:0] out_1
);


  assign out_1 = 22'h1bb000;
endmodule

module beq (
  output [21:0] out_1
);


  assign out_1 = 22'h1d0850;
endmodule

module bne (
  output [21:0] out_1
);


  assign out_1 = 22'h1fc952;
endmodule

module lw (
  output [21:0] out_1
);


  assign out_1 = 22'h21ba80;
endmodule

module sw (
  output [21:0] out_1
);


  assign out_1 = 22'h23ec00;
endmodule

module I_Type (
  output [21:0] out_1,
  output [21:0] out_2,
  output [21:0] out_3,
  output [21:0] out_4,
  output [21:0] out_5,
  output [21:0] out_6,
  output [21:0] out_7,
  output [21:0] out_8,
  output [21:0] out_9,
  output [21:0] out_10,
  output [21:0] out_11,
  output [21:0] out_12,
  output [21:0] out_13,
  output [21:0] out_14
);

  andi andi_1 (.out_1(out_1));
  ori ori_1 (.out_1(out_2));
  xori xori_1 (.out_1(out_3));
  eqvi eqvi_1 (.out_1(out_4));
  addi addi_1 (.out_1(out_5));
  slti slti_1 (.out_1(out_6));
  seqi seqi_1 (.out_1(out_7));
  sll sll_1 (.out_1(out_8));
  srl srl_1 (.out_1(out_9));
  ror ror_1 (.out_1(out_10));
  beq beq_1 (.out_1(out_11));
  bne bne_1 (.out_1(out_12));
  lw lw_1 (.out_1(out_13));
  sw sw_1 (.out_1(out_14));
endmodule

module beqz (
  output [21:0] out_1
);


  assign out_1 = 22'h29c954;
endmodule

module bnez (
  output [21:0] out_1
);


  assign out_1 = 22'h29c954;
endmodule

module bltz (
  output [21:0] out_1
);


  assign out_1 = 22'h2dc958;
endmodule

module bgez (
  output [21:0] out_1
);


  assign out_1 = 22'h2fc95a;
endmodule

module bgtz (
  output [21:0] out_1
);


  assign out_1 = 22'h31c95c;
endmodule

module blez (
  output [21:0] out_1
);


  assign out_1 = 22'h33c95e;
endmodule

module jr (
  output [21:0] out_1
);


  assign {out_1[21:4], out_1[0]} = 19'h6bd3c;
endmodule

module jalr (
  output [21:0] out_1
);


  assign out_1 = 22'h37f971;
endmodule

module set (
  output [21:0] out_1
);


  assign out_1 = 22'h39b800;
endmodule

module sset (
  output [21:0] out_1
);


  assign out_1 = 22'h3bb800;
endmodule

module B_Type (
  output [21:0] out_1,
  output [21:0] out_2,
  output [21:0] out_3,
  output [21:0] out_4,
  output [21:0] out_5,
  output [21:0] out_6,
  output [21:0] out_7,
  output [21:0] out_8,
  output [21:0] out_9,
  output [21:0] out_10
);

  beqz beqz_1 (.out_1(out_1));
  bnez bnez_1 (.out_1(out_2));
  bltz bltz_1 (.out_1(out_3));
  bgez bgez_1 (.out_1(out_4));
  bgtz bgtz_1 (.out_1(out_5));
  blez blez_1 (.out_1(out_6));
  jr jr_1 (.out_1(out_7));
  jalr jalr_1 (.out_1(out_8));
  set set_1 (.out_1(out_9));
  sset sset_1 (.out_1(out_10));
endmodule
