// Logisim project SINGLE-CYCLE PROCESSOR.circ as structural Verilog: 40 circuits, main circuit main
module main (
  input  in_1,
  input  clear,
  output over_flow_flag
);

  wire alu_src, and_1_out, beq, bne_out, bnq, branch, cin, clock_1_out, en, M_read, M_write, REG_WRITE;
  wire [1:0] Memtoreg, pcnext, reg_des, shift_sel;
  wire [3:0] ALU_OP, frist_selector, multiplexer_1_out, sec_selector;
  wire [23:0] _0_23_j_type, adder_1_out, adder_2_out, bit_extender_1_out, multiplexer_2_out,
       multiplexer_3_out, mux_next_pc, register_1_q;
  wire [31:0] alu_out, bit_extender_2_out, bit_extender_3_out, data_in, multiplexer_6_out, ram_2_data,
       rs_data, rt_data, shifter_1_out;

  Clock clock_1 (.out(clock_1_out));
  Register #(.width(24)) register_1 (.D(mux_next_pc), .en(en), .Q(register_1_q), .clk(clock_1_out), .clr(clear));
  Adder #(.width(24)) adder_1 (.a(register_1_q), .b(24'h1), .out(adder_1_out), .cin(1'b0));  // open: cout
  RAM #(.addrWidth(24), .dataWidth(32)) ram_1 (
    .addr(register_1_q), .data({frist_selector, sec_selector, _0_23_j_type}), .clk(clock_1_out), .ld(1'b1),
    .clr(in_1));  // open: sel
  assign bit_extender_1_out = {{8{1'b0}}, _0_23_j_type[15:0]};  // Bit_Extender bit_extender_1
  Multiplexer #(.select(2), .width(4), .enable("false")) multiplexer_1 (
    .in0(_0_23_j_type[19:16]), .in1(_0_23_j_type[15:12]), .in2(4'b1111), .out(multiplexer_1_out),
    .sel(reg_des));  // open: in3
  and and_1 (and_1_out, branch, beq);
  Adder #(.width(24)) adder_2 (.a(adder_1_out), .b(bit_extender_1_out), .out(adder_2_out));  // open: cin, cout
  reg_file reg_file_1 (
    .Ra(_0_23_j_type[23:20]), .Rb(_0_23_j_type[19:16]), .RW(multiplexer_1_out), .BUS_W(multiplexer_6_out),
    .clock(clock_1_out), .read___write(REG_WRITE), .bus_a(rs_data), .bus_B(data_in));
  Multiplexer #(.width(24), .enable("false")) multiplexer_2 (
    .in0(adder_1_out), .in1(adder_2_out), .out(multiplexer_2_out), .sel(and_1_out));
  Multiplexer #(.width(24), .enable("false")) multiplexer_3 (
    .in0(adder_1_out), .in1(adder_2_out), .out(multiplexer_3_out), .sel(bne_out));
  and bne (bne_out, bnq, branch);
  Multiplexer #(.width(32), .enable("false")) multiplexer_4 (
    .in0(data_in), .in1(bit_extender_2_out), .out(rt_data), .sel(alu_src));
  assign bit_extender_2_out = {{16{_0_23_j_type[15]}}, _0_23_j_type[15:0]};  // Bit_Extender bit_extender_2
  Shifter #(.width(32)) shifter_1 (.in(bit_extender_2_out), .\dist (5'b10000), .out(shifter_1_out));
  Multiplexer #(.select(2), .width(24), .enable("false")) multiplexer_5 (
    .in0(multiplexer_2_out), .in1(_0_23_j_type), .in2(rs_data[23:0]), .in3(multiplexer_3_out),
    .out(mux_next_pc), .sel(pcnext));
  assign bit_extender_3_out = {{8{1'b0}}, adder_1_out};  // Bit_Extender bit_extender_3
  control_unit control_unit_1 (
    .sec_input(sec_selector), .frist_input(frist_selector), .alu_op(ALU_OP), .en(en), .regdest(reg_des),
    .re_wr(REG_WRITE), .alu_src(alu_src), .mem_write(M_write), .mem_read(M_read), .mem_to_reg(Memtoreg),
    .pc_next(pcnext), .branch(branch), .c_in(cin), .shift_select(shift_sel));
  ALU ALU (
    .RS_DATA(rs_data), .RT_DATA(rt_data), .SA(_0_23_j_type[4:0]), .IMEADIATE(shifter_1_out), .cin(cin),
    .shift_selector(shift_sel), .ALU_Selector(ALU_OP), .output_of_ALU(alu_out), .out_9(over_flow_flag),
    .Bne(bnq), .Beq(beq));
  RAM #(.addrWidth(24), .dataWidth(32), .bus("separate")) ram_2 (
    .addr(alu_out[23:0]), .din(data_in), .data(ram_2_data), .str(M_write), .clk(clock_1_out), .ld(M_read));  // open: sel, clr
  Multiplexer #(.select(2), .width(32), .enable("false")) multiplexer_6 (
    .in0(alu_out), .in1(ram_2_data), .in2(bit_extender_3_out), .out(multiplexer_6_out), .sel(Memtoreg));  // open: in3

  // Notes on the sheet:
  //   PC
  //   INSTRUCTION MEMO
  //   j-type
  //   RS
  //   rd
  //   reg-dest
  //   RT
  //   I-TYPE
  //   cu
  //   BUS A
  //   BUS B
  //   branch
  //   pc-next
  //   alu-src
  //   mem-reg
endmodule

// REG FILE
module reg_file (
  input  [3:0] Ra,
  input  [3:0] Rb,
  input  [3:0] RW,
  input  [31:0] BUS_W,
  input  clock,
  input  read___write,
  output [31:0] bus_a,
  output [31:0] bus_B
);

  wire and_1_out, and_2_out, and_3_out, and_4_out, and_5_out, and_6_out, and_7_out, and_8_out, and_9_out,
       and_10_out, and_11_out, and_12_out, and_13_out, and_14_out, and_15_out, decoder_1_out1,
       decoder_1_out2, decoder_1_out3, decoder_1_out4, decoder_1_out5, decoder_1_out6, decoder_1_out7,
       decoder_1_out8, decoder_1_out9, decoder_1_out10, decoder_1_out11, decoder_1_out12, decoder_1_out13,
       decoder_1_out14, decoder_1_out15, decoder_2_out0, decoder_2_out1, decoder_2_out2, decoder_2_out3,
       decoder_2_out4, decoder_2_out5, decoder_2_out6, decoder_2_out7, decoder_2_out8, decoder_2_out9,
       decoder_2_out10, decoder_2_out11, decoder_2_out12, decoder_2_out13, decoder_2_out14, decoder_2_out15,
       decoder_3_out0, decoder_3_out1, decoder_3_out2, decoder_3_out3, decoder_3_out4, decoder_3_out5,
       decoder_3_out6, decoder_3_out7, decoder_3_out8, decoder_3_out9, decoder_3_out10, decoder_3_out11,
       decoder_3_out12, decoder_3_out13, decoder_3_out14, decoder_3_out15;
  wire [31:0] register_1_q, register_2_q, register_3_q, register_4_q, register_5_q, register_6_q,
       register_7_q, register_8_q, register_9_q, register_10_q, register_11_q, register_12_q, register_13_q,
       register_14_q, register_15_q;

  Decoder #(.select(4)) decoder_1 (
    .out1(decoder_1_out1), .out2(decoder_1_out2), .out3(decoder_1_out3), .out4(decoder_1_out4),
    .out5(decoder_1_out5), .out6(decoder_1_out6), .out7(decoder_1_out7), .out8(decoder_1_out8),
    .out9(decoder_1_out9), .out10(decoder_1_out10), .out11(decoder_1_out11), .out12(decoder_1_out12),
    .out13(decoder_1_out13), .out14(decoder_1_out14), .out15(decoder_1_out15), .sel(RW));  // open: out0, en
  and and_1 (and_1_out, decoder_1_out1, read___write);
  and and_2 (and_2_out, decoder_1_out2, read___write);
  and and_3 (and_3_out, decoder_1_out3, read___write);
  and and_4 (and_4_out, decoder_1_out4, read___write);
  and and_5 (and_5_out, decoder_1_out5, read___write);
  and and_6 (and_6_out, decoder_1_out6, read___write);
  and and_7 (and_7_out, decoder_1_out7, read___write);
  and and_8 (and_8_out, decoder_1_out8, read___write);
  and and_9 (and_9_out, decoder_1_out9, read___write);
  and and_10 (and_10_out, decoder_1_out10, read___write);
  and and_11 (and_11_out, decoder_1_out11, read___write);
  and and_12 (and_12_out, decoder_1_out12, read___write);
  and and_13 (and_13_out, decoder_1_out13, read___write);
  and and_14 (and_14_out, decoder_1_out14, read___write);
  and and_15 (and_15_out, decoder_1_out15, read___write);
  Register #(.width(32)) register_1 (.D(BUS_W), .en(and_1_out), .Q(register_1_q), .clk(clock));  // open: clr
  Register #(.width(32)) register_2 (.D(BUS_W), .en(and_2_out), .Q(register_2_q), .clk(clock));  // open: clr
  Register #(.width(32)) register_3 (.D(BUS_W), .en(and_3_out), .Q(register_3_q), .clk(clock));  // open: clr
  Register #(.width(32)) register_4 (.D(BUS_W), .en(and_4_out), .Q(register_4_q), .clk(clock));  // open: clr
  Register #(.width(32)) register_5 (.D(BUS_W), .en(and_5_out), .Q(register_5_q), .clk(clock));  // open: clr
  Register #(.width(32)) register_6 (.D(BUS_W), .en(and_6_out), .Q(register_6_q), .clk(clock));  // open: clr
  Register #(.width(32)) register_7 (.D(BUS_W), .en(and_7_out), .Q(register_7_q), .clk(clock));  // open: clr
  Register #(.width(32)) register_8 (.D(BUS_W), .en(and_8_out), .Q(register_8_q), .clk(clock));  // open: clr
  Register #(.width(32)) register_9 (.D(BUS_W), .en(and_9_out), .Q(register_9_q), .clk(clock));  // open: clr
  Register #(.width(32)) register_10 (.D(BUS_W), .en(and_10_out), .Q(register_10_q), .clk(clock));  // open: clr
  Register #(.width(32)) register_11 (.D(BUS_W), .en(and_11_out), .Q(register_11_q), .clk(clock));  // open: clr
  Register #(.width(32)) register_12 (.D(BUS_W), .en(and_12_out), .Q(register_12_q), .clk(clock));  // open: clr
  Register #(.width(32)) register_13 (.D(BUS_W), .en(and_13_out), .Q(register_13_q), .clk(clock));  // open: clr
  Register #(.width(32)) register_14 (.D(BUS_W), .en(and_14_out), .Q(register_14_q), .clk(clock));  // open: clr
  Register #(.width(32)) register_15 (.D(BUS_W), .en(and_15_out), .Q(register_15_q), .clk(clock));  // open: clr
  Decoder #(.select(4)) decoder_2 (
    .out0(decoder_2_out0), .out1(decoder_2_out1), .out2(decoder_2_out2), .out3(decoder_2_out3),
    .out4(decoder_2_out4), .out5(decoder_2_out5), .out6(decoder_2_out6), .out7(decoder_2_out7),
    .out8(decoder_2_out8), .out9(decoder_2_out9), .out10(decoder_2_out10), .out11(decoder_2_out11),
    .out12(decoder_2_out12), .out13(decoder_2_out13), .out14(decoder_2_out14), .out15(decoder_2_out15),
    .sel(Ra));  // open: en
  assign bus_a = decoder_2_out8 ? register_8_q : 32'bz;  // Controlled_Buffer controlled_buffer_1
  assign bus_a = decoder_2_out0 ? {32{1'b0}} : 32'bz;  // Controlled_Buffer controlled_buffer_2
  assign bus_a = decoder_2_out1 ? register_1_q : 32'bz;  // Controlled_Buffer controlled_buffer_3
  assign bus_a = decoder_2_out2 ? register_2_q : 32'bz;  // Controlled_Buffer controlled_buffer_4
  assign bus_a = decoder_2_out3 ? register_3_q : 32'bz;  // Controlled_Buffer controlled_buffer_5
  assign bus_a = decoder_2_out4 ? register_4_q : 32'bz;  // Controlled_Buffer controlled_buffer_6
  assign bus_a = decoder_2_out5 ? register_5_q : 32'bz;  // Controlled_Buffer controlled_buffer_7
  assign bus_a = decoder_2_out6 ? register_6_q : 32'bz;  // Controlled_Buffer controlled_buffer_8
  assign bus_a = decoder_2_out7 ? register_7_q : 32'bz;  // Controlled_Buffer controlled_buffer_9
  assign bus_a = decoder_2_out9 ? register_9_q : 32'bz;  // Controlled_Buffer controlled_buffer_10
  assign bus_a = decoder_2_out10 ? register_10_q : 32'bz;  // Controlled_Buffer controlled_buffer_11
  assign bus_a = decoder_2_out11 ? register_11_q : 32'bz;  // Controlled_Buffer controlled_buffer_12
  assign bus_a = decoder_2_out12 ? register_12_q : 32'bz;  // Controlled_Buffer controlled_buffer_13
  assign bus_a = decoder_2_out13 ? register_13_q : 32'bz;  // Controlled_Buffer controlled_buffer_14
  assign bus_a = decoder_2_out14 ? register_14_q : 32'bz;  // Controlled_Buffer controlled_buffer_15
  assign bus_a = decoder_2_out15 ? register_15_q : 32'bz;  // Controlled_Buffer controlled_buffer_16
  Decoder #(.select(4)) decoder_3 (
    .out0(decoder_3_out0), .out1(decoder_3_out1), .out2(decoder_3_out2), .out3(decoder_3_out3),
    .out4(decoder_3_out4), .out5(decoder_3_out5), .out6(decoder_3_out6), .out7(decoder_3_out7),
    .out8(decoder_3_out8), .out9(decoder_3_out9), .out10(decoder_3_out10), .out11(decoder_3_out11),
    .out12(decoder_3_out12), .out13(decoder_3_out13), .out14(decoder_3_out14), .out15(decoder_3_out15),
    .sel(Rb));  // open: en
  assign bus_B = decoder_3_out1 ? register_1_q : 32'bz;  // Controlled_Buffer controlled_buffer_17
  assign bus_B = decoder_3_out2 ? register_2_q : 32'bz;  // Controlled_Buffer controlled_buffer_18
  assign bus_B = decoder_3_out3 ? register_3_q : 32'bz;  // Controlled_Buffer controlled_buffer_19
  assign bus_B = decoder_3_out4 ? register_4_q : 32'bz;  // Controlled_Buffer controlled_buffer_20
  assign bus_B = decoder_3_out5 ? register_5_q : 32'bz;  // Controlled_Buffer controlled_buffer_21
  assign bus_B = decoder_3_out6 ? register_6_q : 32'bz;  // Controlled_Buffer controlled_buffer_22
  assign bus_B = decoder_3_out7 ? register_7_q : 32'bz;  // Controlled_Buffer controlled_buffer_23
  assign bus_B = decoder_3_out8 ? register_8_q : 32'bz;  // Controlled_Buffer controlled_buffer_24
  assign bus_B = decoder_3_out9 ? register_9_q : 32'bz;  // Controlled_Buffer controlled_buffer_25
  assign bus_B = decoder_3_out10 ? register_10_q : 32'bz;  // Controlled_Buffer controlled_buffer_26
  assign bus_B = decoder_3_out11 ? register_11_q : 32'bz;  // Controlled_Buffer controlled_buffer_27
  assign bus_B = decoder_3_out12 ? register_12_q : 32'bz;  // Controlled_Buffer controlled_buffer_28
  assign bus_B = decoder_3_out13 ? register_13_q : 32'bz;  // Controlled_Buffer controlled_buffer_29
  assign bus_B = decoder_3_out14 ? register_14_q : 32'bz;  // Controlled_Buffer controlled_buffer_30
  assign bus_B = decoder_3_out15 ? register_15_q : 32'bz;  // Controlled_Buffer controlled_buffer_31
  assign bus_B = decoder_3_out0 ? {32{1'b0}} : 32'bz;  // Controlled_Buffer controlled_buffer_32

  // Notes on the sheet:
  //   RW: pull=down
endmodule

module ALU (
  input  [31:0] RS_DATA,
  input  [3:0] ALU_Selector,
  input  [31:0] RT_DATA,
  input  [4:0] SA,
  input  [1:0] shift_selector,
  input  [31:0] IMEADIATE,
  input  cin,
  output [31:0] output_of_ALU,
  output out_9,
  output Bne,
  output Beq
);

  wire comparator_1_lt, comparator_2_lt;
  wire [31:0] adder_subtractor_1_result, and_1_out, and_2_out, bit_extender_1_out, bit_extender_2_out,
       bit_extender_3_out, bit_extender_4_out, multiplexer_1_out, or_1_out, or_2_out, shifter_1_out,
       shifter_2_out, shifter_3_out, shifter_4_out, xnor_1_out, xor_1_out;

  adder__subtractor adder_subtractor_1 (
    .RS_DATA(RS_DATA), .in_2(cin), .RT_DATA(RT_DATA), .result(adder_subtractor_1_result), .overflow(out_9));  // open: C31, C1
  Comparator #(.width(32)) comparator_1 (.a(RS_DATA), .b(RT_DATA), .eq(Beq), .lt(comparator_1_lt));  // open: gt
  Comparator #(.width(32), .mode("unsigned")) comparator_2 (
    .a(RS_DATA), .b(RT_DATA), .lt(comparator_2_lt));  // open: gt, eq
  assign and_1_out = RS_DATA & RT_DATA;  // AND_Gate and_1, 32 bits wide
  assign or_1_out = RS_DATA | RT_DATA;  // OR_Gate or_1, 32 bits wide
  assign xor_1_out = RS_DATA ^ RT_DATA;  // XOR_Gate xor_1, 32 bits wide
  assign xnor_1_out = ~(RS_DATA ^ RT_DATA);  // XNOR_Gate xnor_1, 32 bits wide
  Shifter #(.width(32)) shifter_1 (.in(RS_DATA), .\dist (SA), .out(shifter_1_out));
  Shifter #(.width(32), .shift("lr")) shifter_2 (.in(RS_DATA), .\dist (SA), .out(shifter_2_out));
  Shifter #(.width(32), .shift("ar")) shifter_3 (.in(RS_DATA), .\dist (SA), .out(shifter_3_out));
  Shifter #(.width(32), .shift("rr")) shifter_4 (.in(RS_DATA), .\dist (SA), .out(shifter_4_out));
  assign and_2_out = RS_DATA & 32'hffff;  // AND_Gate and_2, 32 bits wide
  assign bit_extender_1_out = {{31{1'b0}}, Bne};  // Bit_Extender bit_extender_1
  not not_1 (Bne, Beq);
  assign bit_extender_2_out = {{31{1'b0}}, comparator_2_lt};  // Bit_Extender bit_extender_2
  assign or_2_out = and_2_out | IMEADIATE;  // OR_Gate or_2, 32 bits wide
  assign bit_extender_3_out = {{31{1'b0}}, comparator_1_lt};  // Bit_Extender bit_extender_3
  Multiplexer #(.select(2), .width(32)) multiplexer_1 (
    .in0(shifter_1_out), .in1(shifter_2_out), .in2(shifter_3_out), .in3(shifter_4_out),
    .out(multiplexer_1_out), .sel(shift_selector));  // open: en
  assign bit_extender_4_out = {{31{1'b0}}, Beq};  // Bit_Extender bit_extender_4
  Multiplexer #(.select(4), .width(32)) multiplexer_2 (
    .in0(and_1_out), .in1(or_1_out), .in2(xor_1_out), .in3(adder_subtractor_1_result), .in4(xnor_1_out),
    .in5(multiplexer_1_out), .in6(or_2_out), .in7(bit_extender_3_out), .in8(bit_extender_2_out),
    .in9(bit_extender_1_out), .in10(bit_extender_4_out), .in11({32{1'b0}}), .in12({32{1'b0}}),
    .in13({32{1'b0}}), .in14({32{1'b0}}), .in15({32{1'b0}}), .out(output_of_ALU), .sel(ALU_Selector));  // open: en
endmodule

module control_unit (
  input  [3:0] sec_input,
  input  [3:0] frist_input,
  output [3:0] alu_op,
  output en,
  output [1:0] regdest,
  output re_wr,
  output alu_src,
  output mem_write,
  output mem_read,
  output [1:0] mem_to_reg,
  output [1:0] pc_next,
  output branch,
  output c_in,
  output [1:0] shift_select
);

  wire [18:0] exit, type_1_1_out_2, type_2_1_out_2, type_3_1_out_2, type_4_1_out_2, type_5_1_out_2,
       type_6_1_out_2;

  exit_6 exit_6_1 (
    .alu_op(exit[3:0]), .en(exit[4]), .regdest(exit[6:5]), .re_wr(exit[7]), .alu_src(exit[8]),
    .mem_write(exit[9]), .mem_read(exit[10]), .mem_to_reg(exit[12:11]), .pc_next(exit[14:13]),
    .branch(exit[15]), .c_in(exit[16]), .shift_select(exit[18:17]));
  type_1 type_1_1 (.\input (sec_input), .out_2(type_1_1_out_2));
  type_2 type_2_1 (.\input (sec_input), .out_2(type_2_1_out_2));
  type_3 type_3_1 (.\input (sec_input), .out_2(type_3_1_out_2));
  type_4 type_4_1 (.\input (sec_input), .out_2(type_4_1_out_2));
  type_5 type_5_1 (.\input (sec_input), .out_2(type_5_1_out_2));
  type_6 type_6_1 (.\input (sec_input), .out_2(type_6_1_out_2));
  Multiplexer #(.select(4), .width(19), .enable("false")) multiplexer_1 (
    .in0(type_1_1_out_2), .in1(type_2_1_out_2), .in2(type_3_1_out_2), .in3(type_4_1_out_2),
    .in4(type_5_1_out_2), .in5(type_6_1_out_2), .in6(exit), .in7({19{1'b0}}), .in8({19{1'b0}}),
    .in9({19{1'b0}}), .in10({19{1'b0}}), .in11({19{1'b0}}), .in12({19{1'b0}}), .in13({19{1'b0}}),
    .in14({19{1'b0}}), .in15({19{1'b0}}),
    .out({shift_select, c_in, branch, pc_next, mem_to_reg, mem_read, mem_write, alu_src, re_wr, regdest, en, alu_op}),
    .sel(frist_input));
endmodule

module adder__subtractor (
  input  [31:0] RS_DATA,
  input  in_2,
  input  [31:0] RT_DATA,
  output [31:0] result,
  output C31,
  output C1,
  output overflow
);

  wire inputB1;
  wire [30:0] inputB31;
  wire [31:0] bit_extender_1_out;

  assign bit_extender_1_out = {{31{in_2}}, in_2};  // Bit_Extender bit_extender_1
  assign inputB31 = bit_extender_1_out[30:0] ^ RT_DATA[30:0];  // XOR_Gate xor_1, 31 bits wide
  xor xor_2 (inputB1, bit_extender_1_out[31], RT_DATA[31]);
  Adder #(.width(31)) adder_1 (.a(RS_DATA[30:0]), .b(inputB31), .out(result[30:0]), .cin(in_2), .cout(C31));
  Adder #(.width(1)) adder_2 (.a(RS_DATA[31]), .b(inputB1), .out(result[31]), .cin(C31), .cout(C1));
  xor xor_3 (overflow, C31, C1);

  // Other names for the same wires on the sheet: inputA31[30:0] = RS_DATA[30:0]; inputA1 = RS_DATA[31]
endmodule

module add1 (
  output [3:0] alu_op,
  output en,
  output [1:0] regdest,
  output re_wr,
  output alu_src,
  output mem_write,
  output mem_read,
  output [1:0] mem_to_reg,
  output [1:0] pc_next,
  output branch,
  output c_in,
  output [1:0] shift_select
);


  assign alu_op = 4'b0011;
  assign alu_src = 1'b0;
  assign branch = 1'b0;
  assign c_in = 1'b0;
  assign en = 1'b1;
  assign mem_read = 1'b0;
  assign mem_to_reg = 2'b00;
  assign mem_write = 1'b0;
  assign pc_next = 2'b00;
  assign re_wr = 1'b1;
  assign regdest = 2'b01;
  assign shift_select = 2'b00;
endmodule

module sub1 (
  output [3:0] alu_op,
  output en,
  output [1:0] regdest,
  output re_wr,
  output alu_src,
  output mem_write,
  output mem_read,
  output [1:0] mem_to_reg,
  output [1:0] pc_next,
  output branch,
  output c_in,
  output [1:0] shift_select
);


  assign alu_op = 4'b0011;
  assign alu_src = 1'b0;
  assign branch = 1'b0;
  assign c_in = 1'b1;
  assign en = 1'b1;
  assign mem_read = 1'b0;
  assign mem_to_reg = 2'b00;
  assign mem_write = 1'b0;
  assign pc_next = 2'b00;
  assign re_wr = 1'b1;
  assign regdest = 2'b01;
  assign shift_select = 2'b00;
endmodule

module slt1 (
  output [3:0] alu_op,
  output en,
  output [1:0] regdest,
  output re_wr,
  output alu_src,
  output mem_write,
  output mem_read,
  output [1:0] mem_to_reg,
  output [1:0] pc_next,
  output branch,
  output c_in,
  output [1:0] shift_select
);


  assign alu_op = 4'b0111;
  assign alu_src = 1'b0;
  assign branch = 1'b0;
  assign c_in = 1'b0;
  assign en = 1'b1;
  assign mem_read = 1'b0;
  assign mem_to_reg = 2'b00;
  assign mem_write = 1'b0;
  assign pc_next = 2'b00;
  assign re_wr = 1'b1;
  assign regdest = 2'b01;
  assign shift_select = 2'b00;
endmodule

module sltu1 (
  output [3:0] alu_op,
  output en,
  output [1:0] regdest,
  output re_wr,
  output alu_src,
  output mem_write,
  output mem_read,
  output [1:0] mem_to_reg,
  output [1:0] pc_next,
  output branch,
  output c_in,
  output [1:0] shift_select
);


  assign alu_op = 4'b1000;
  assign alu_src = 1'b0;
  assign branch = 1'b0;
  assign c_in = 1'b0;
  assign en = 1'b1;
  assign mem_read = 1'b0;
  assign mem_to_reg = 2'b00;
  assign mem_write = 1'b0;
  assign pc_next = 2'b00;
  assign re_wr = 1'b1;
  assign regdest = 2'b01;
  assign shift_select = 2'b00;
endmodule

module and1 (
  output [3:0] alu_op,
  output en,
  output [1:0] regdest,
  output re_wr,
  output alu_src,
  output mem_write,
  output mem_read,
  output [1:0] mem_to_reg,
  output [1:0] pc_next,
  output branch,
  output c_in,
  output [1:0] shift_select
);


  assign alu_op = 4'b0000;
  assign alu_src = 1'b0;
  assign branch = 1'b0;
  assign c_in = 1'b0;
  assign en = 1'b1;
  assign mem_read = 1'b0;
  assign mem_to_reg = 2'b00;
  assign mem_write = 1'b0;
  assign pc_next = 2'b00;
  assign re_wr = 1'b1;
  assign regdest = 2'b01;
  assign shift_select = 2'b00;
endmodule

module or1 (
  output [3:0] alu_op,
  output en,
  output [1:0] regdest,
  output re_wr,
  output alu_src,
  output mem_write,
  output mem_read,
  output [1:0] mem_to_reg,
  output [1:0] pc_next,
  output branch,
  output c_in,
  output [1:0] shift_select
);


  assign alu_op = 4'b0001;
  assign alu_src = 1'b0;
  assign branch = 1'b0;
  assign c_in = 1'b0;
  assign en = 1'b1;
  assign mem_read = 1'b0;
  assign mem_to_reg = 2'b00;
  assign mem_write = 1'b0;
  assign pc_next = 2'b00;
  assign re_wr = 1'b1;
  assign regdest = 2'b01;
  assign shift_select = 2'b00;
endmodule

module \xor  (
  output [3:0] alu_op,
  output en,
  output [1:0] regdest,
  output re_wr,
  output alu_src,
  output mem_write,
  output mem_read,
  output [1:0] mem_to_reg,
  output [1:0] pc_next,
  output branch,
  output c_in,
  output [1:0] shift_select
);


  assign alu_op = 4'b0010;
  assign alu_src = 1'b0;
  assign branch = 1'b0;
  assign c_in = 1'b0;
  assign en = 1'b1;
  assign mem_read = 1'b0;
  assign mem_to_reg = 2'b00;
  assign mem_write = 1'b0;
  assign pc_next = 2'b00;
  assign re_wr = 1'b1;
  assign regdest = 2'b01;
  assign shift_select = 2'b00;
endmodule

module eqv1 (
  output [3:0] alu_op,
  output en,
  output [1:0] regdest,
  output re_wr,
  output alu_src,
  output mem_write,
  output mem_read,
  output [1:0] mem_to_reg,
  output [1:0] pc_next,
  output branch,
  output c_in,
  output [1:0] shift_select
);


  assign alu_op = 4'b0100;
  assign alu_src = 1'b0;
  assign branch = 1'b0;
  assign c_in = 1'b0;
  assign en = 1'b1;
  assign mem_read = 1'b0;
  assign mem_to_reg = 2'b00;
  assign mem_write = 1'b0;
  assign pc_next = 2'b00;
  assign re_wr = 1'b1;
  assign regdest = 2'b01;
  assign shift_select = 2'b00;
endmodule

module sra1 (
  output [3:0] alu_op,
  output en,
  output [1:0] regdest,
  output re_wr,
  output alu_src,
  output mem_write,
  output mem_read,
  output [1:0] mem_to_reg,
  output [1:0] pc_next,
  output branch,
  output c_in,
  output [1:0] shift_select
);


  assign alu_op = 4'b0101;
  assign alu_src = 1'b1;
  assign branch = 1'b0;
  assign c_in = 1'b0;
  assign en = 1'b1;
  assign mem_read = 1'b0;
  assign mem_to_reg = 2'b00;
  assign mem_write = 1'b0;
  assign pc_next = 2'b00;
  assign re_wr = 1'b1;
  assign regdest = 2'b00;
  assign shift_select = 2'b10;
endmodule

module type_1 (
  input  [3:0] \input ,
  output [18:0] out_2
);

  wire [18:0] add, \and , eqv, \or , slt, sltu, sub, \xor ;

  add1 add1_1 (
    .alu_op(add[3:0]), .en(add[4]), .regdest(add[6:5]), .re_wr(add[7]), .alu_src(add[8]), .mem_write(add[9]),
    .mem_read(add[10]), .mem_to_reg(add[12:11]), .pc_next(add[14:13]), .branch(add[15]), .c_in(add[16]),
    .shift_select(add[18:17]));
  sltu1 sltu1_1 (
    .alu_op(sltu[3:0]), .en(sltu[4]), .regdest(sltu[6:5]), .re_wr(sltu[7]), .alu_src(sltu[8]),
    .mem_write(sltu[9]), .mem_read(sltu[10]), .mem_to_reg(sltu[12:11]), .pc_next(sltu[14:13]),
    .branch(sltu[15]), .c_in(sltu[16]), .shift_select(sltu[18:17]));
  \xor  xor_1 (
    .alu_op(\xor [3:0]), .en(\xor [4]), .regdest(\xor [6:5]), .re_wr(\xor [7]), .alu_src(\xor [8]),
    .mem_write(\xor [9]), .mem_read(\xor [10]), .mem_to_reg(\xor [12:11]), .pc_next(\xor [14:13]),
    .branch(\xor [15]), .c_in(\xor [16]), .shift_select(\xor [18:17]));
  sub1 sub1_1 (
    .alu_op(sub[3:0]), .en(sub[4]), .regdest(sub[6:5]), .re_wr(sub[7]), .alu_src(sub[8]), .mem_write(sub[9]),
    .mem_read(sub[10]), .mem_to_reg(sub[12:11]), .pc_next(sub[14:13]), .branch(sub[15]), .c_in(sub[16]),
    .shift_select(sub[18:17]));
  and1 and1_1 (
    .alu_op(\and [3:0]), .en(\and [4]), .regdest(\and [6:5]), .re_wr(\and [7]), .alu_src(\and [8]),
    .mem_write(\and [9]), .mem_read(\and [10]), .mem_to_reg(\and [12:11]), .pc_next(\and [14:13]),
    .branch(\and [15]), .c_in(\and [16]), .shift_select(\and [18:17]));
  eqv1 eqv1_1 (
    .alu_op(eqv[3:0]), .en(eqv[4]), .regdest(eqv[6:5]), .re_wr(eqv[7]), .alu_src(eqv[8]), .mem_write(eqv[9]),
    .mem_read(eqv[10]), .mem_to_reg(eqv[12:11]), .pc_next(eqv[14:13]), .branch(eqv[15]), .c_in(eqv[16]),
    .shift_select(eqv[18:17]));
  slt1 slt1_1 (
    .alu_op(slt[3:0]), .en(slt[4]), .regdest(slt[6:5]), .re_wr(slt[7]), .alu_src(slt[8]), .mem_write(slt[9]),
    .mem_read(slt[10]), .mem_to_reg(slt[12:11]), .pc_next(slt[14:13]), .branch(slt[15]), .c_in(slt[16]),
    .shift_select(slt[18:17]));
  or1 or1_1 (
    .alu_op(\or [3:0]), .en(\or [4]), .regdest(\or [6:5]), .re_wr(\or [7]), .alu_src(\or [8]),
    .mem_write(\or [9]), .mem_read(\or [10]), .mem_to_reg(\or [12:11]), .pc_next(\or [14:13]),
    .branch(\or [15]), .c_in(\or [16]), .shift_select(\or [18:17]));
  Multiplexer #(.select(4), .width(19)) multiplexer_1 (
    .in0(add), .in1(sub), .in2(slt), .in3(sltu), .in4(\and ), .in5(\or ), .in6(\xor ), .in7(eqv),
    .in8({19{1'b0}}), .in9({19{1'b0}}), .in10({19{1'b0}}), .in11({19{1'b0}}), .in12({19{1'b0}}),
    .in13({19{1'b0}}), .in14({19{1'b0}}), .in15({19{1'b0}}), .out(out_2), .sel(\input ));  // open: en
endmodule

module addi2 (
  output [3:0] alu_op,
  output en,
  output [1:0] regdest,
  output re_wr,
  output alu_src,
  output mem_write,
  output mem_read,
  output [1:0] mem_to_reg,
  output [1:0] pc_next,
  output branch,
  output c_in,
  output [1:0] shift_select
);


  assign alu_op = 4'b0011;
  assign alu_src = 1'b1;
  assign branch = 1'b0;
  assign c_in = 1'b0;
  assign en = 1'b1;
  assign mem_read = 1'b0;
  assign mem_to_reg = 2'b00;
  assign mem_write = 1'b0;
  assign pc_next = 2'b00;
  assign re_wr = 1'b1;
  assign regdest = 2'b00;
  assign shift_select = 2'b00;
endmodule

module slti2 (
  output [3:0] alu_op,
  output en,
  output [1:0] regdest,
  output re_wr,
  output alu_src,
  output mem_write,
  output mem_read,
  output [1:0] mem_to_reg,
  output [1:0] pc_next,
  output branch,
  output c_in,
  output [1:0] shift_select
);


  assign alu_op = 4'b0111;
  assign alu_src = 1'b1;
  assign branch = 1'b0;
  assign c_in = 1'b0;
  assign en = 1'b1;
  assign mem_read = 1'b0;
  assign mem_to_reg = 2'b00;
  assign mem_write = 1'b0;
  assign pc_next = 2'b00;
  assign re_wr = 1'b1;
  assign regdest = 2'b00;
  assign shift_select = 2'b00;
endmodule

module sltiu2 (
  output [3:0] alu_op,
  output en,
  output [1:0] regdest,
  output re_wr,
  output alu_src,
  output mem_write,
  output mem_read,
  output [1:0] mem_to_reg,
  output [1:0] pc_next,
  output branch,
  output c_in,
  output [1:0] shift_select
);


  assign alu_op = 4'b1000;
  assign alu_src = 1'b1;
  assign branch = 1'b0;
  assign c_in = 1'b0;
  assign en = 1'b1;
  assign mem_read = 1'b0;
  assign mem_to_reg = 2'b00;
  assign mem_write = 1'b0;
  assign pc_next = 2'b00;
  assign re_wr = 1'b1;
  assign regdest = 2'b00;
  assign shift_select = 2'b00;
endmodule

module andi2 (
  output [3:0] alu_op,
  output en,
  output [1:0] regdest,
  output re_wr,
  output alu_src,
  output mem_write,
  output mem_read,
  output [1:0] mem_to_reg,
  output [1:0] pc_next,
  output branch,
  output c_in,
  output [1:0] shift_select
);


  assign alu_op = 4'b0000;
  assign alu_src = 1'b1;
  assign branch = 1'b0;
  assign c_in = 1'b0;
  assign en = 1'b1;
  assign mem_read = 1'b0;
  assign mem_to_reg = 2'b00;
  assign mem_write = 1'b0;
  assign pc_next = 2'b00;
  assign re_wr = 1'b1;
  assign regdest = 2'b00;
  assign shift_select = 2'b00;
endmodule

module ori2 (
  output [3:0] alu_op,
  output en,
  output [1:0] regdest,
  output re_wr,
  output alu_src,
  output mem_write,
  output mem_read,
  output [1:0] mem_to_reg,
  output [1:0] pc_next,
  output branch,
  output c_in,
  output [1:0] shift_select
);


  assign alu_op = 4'b0001;
  assign alu_src = 1'b1;
  assign branch = 1'b0;
  assign c_in = 1'b0;
  assign en = 1'b1;
  assign mem_read = 1'b0;
  assign mem_to_reg = 2'b00;
  assign mem_write = 1'b0;
  assign pc_next = 2'b00;
  assign re_wr = 1'b1;
  assign regdest = 2'b00;
  assign shift_select = 2'b00;
endmodule

module xori2 (
  output [3:0] alu_op,
  output en,
  output [1:0] regdest,
  output re_wr,
  output alu_src,
  output mem_write,
  output mem_read,
  output [1:0] mem_to_reg,
  output [1:0] pc_next,
  output branch,
  output c_in,
  output [1:0] shift_select
);


  assign alu_op = 4'b0010;
  assign alu_src = 1'b1;
  assign branch = 1'b0;
  assign c_in = 1'b0;
  assign en = 1'b1;
  assign mem_read = 1'b0;
  assign mem_to_reg = 2'b00;
  assign mem_write = 1'b0;
  assign pc_next = 2'b00;
  assign re_wr = 1'b1;
  assign regdest = 2'b00;
  assign shift_select = 2'b00;
endmodule

module eqvi2 (
  output [3:0] alu_op,
  output en,
  output [1:0] regdest,
  output re_wr,
  output alu_src,
  output mem_write,
  output mem_read,
  output [1:0] mem_to_reg,
  output [1:0] pc_next,
  output branch,
  output c_in,
  output [1:0] shift_select
);


  assign alu_op = 4'b0100;
  assign alu_src = 1'b1;
  assign branch = 1'b0;
  assign c_in = 1'b0;
  assign en = 1'b1;
  assign mem_read = 1'b0;
  assign mem_to_reg = 2'b00;
  assign mem_write = 1'b0;
  assign pc_next = 2'b00;
  assign re_wr = 1'b1;
  assign regdest = 2'b00;
  assign shift_select = 2'b00;
endmodule

module sll2 (
  output [3:0] alu_op,
  output en,
  output [1:0] regdest,
  output re_wr,
  output alu_src,
  output mem_write,
  output mem_read,
  output [1:0] mem_to_reg,
  output [1:0] pc_next,
  output branch,
  output c_in,
  output [1:0] shift_select
);


  assign alu_op = 4'b0101;
  assign alu_src = 1'b1;
  assign branch = 1'b0;
  assign c_in = 1'b0;
  assign en = 1'b1;
  assign mem_read = 1'b0;
  assign mem_to_reg = 2'b00;
  assign mem_write = 1'b0;
  assign pc_next = 2'b00;
  assign re_wr = 1'b1;
  assign regdest = 2'b00;
  assign shift_select = 2'b00;
endmodule

module srl2 (
  output [3:0] alu_op,
  output en,
  output [1:0] regdest,
  output re_wr,
  output alu_src,
  output mem_write,
  output mem_read,
  output [1:0] mem_to_reg,
  output [1:0] pc_next,
  output branch,
  output c_in,
  output [1:0] shift_select
);


  assign alu_op = 4'b0101;
  assign alu_src = 1'b1;
  assign branch = 1'b0;
  assign c_in = 1'b0;
  assign en = 1'b1;
  assign mem_read = 1'b0;
  assign mem_to_reg = 2'b00;
  assign mem_write = 1'b0;
  assign pc_next = 2'b00;
  assign re_wr = 1'b1;
  assign regdest = 2'b00;
  assign shift_select = 2'b01;
endmodule

module ror2 (
  output [3:0] alu_op,
  output en,
  output [1:0] regdest,
  output re_wr,
  output alu_src,
  output mem_write,
  output mem_read,
  output [1:0] mem_to_reg,
  output [1:0] pc_next,
  output branch,
  output c_in,
  output [1:0] shift_select
);


  assign alu_op = 4'b0101;
  assign alu_src = 1'b1;
  assign branch = 1'b0;
  assign c_in = 1'b0;
  assign en = 1'b1;
  assign mem_read = 1'b0;
  assign mem_to_reg = 2'b00;
  assign mem_write = 1'b0;
  assign pc_next = 2'b00;
  assign re_wr = 1'b1;
  assign regdest = 2'b00;
  assign shift_select = 2'b10;
endmodule

module seth2 (
  output [3:0] alu_op,
  output en,
  output [1:0] regdest,
  output re_wr,
  output alu_src,
  output mem_write,
  output mem_read,
  output [1:0] mem_to_reg,
  output [1:0] pc_next,
  output branch,
  output c_in,
  output [1:0] shift_select
);


  assign alu_op = 4'b0110;
  assign alu_src = 1'b1;
  assign branch = 1'b0;
  assign c_in = 1'b0;
  assign en = 1'b1;
  assign mem_read = 1'b0;
  assign mem_to_reg = 2'b00;
  assign mem_write = 1'b0;
  assign pc_next = 2'b00;
  assign re_wr = 1'b1;
  assign regdest = 2'b00;
  assign shift_select = 2'b00;
endmodule

module type_2 (
  input  [3:0] \input ,
  output [18:0] out_2
);

  wire [18:0] addi, andi, eqvi, ori, ror, seth, sll, slti, sltiu, SRA, srl, xori;

  addi2 addi2_1 (
    .alu_op(addi[3:0]), .en(addi[4]), .regdest(addi[6:5]), .re_wr(addi[7]), .alu_src(addi[8]),
    .mem_write(addi[9]), .mem_read(addi[10]), .mem_to_reg(addi[12:11]), .pc_next(addi[14:13]),
    .branch(addi[15]), .c_in(addi[16]), .shift_select(addi[18:17]));
  andi2 andi2_1 (
    .alu_op(andi[3:0]), .en(andi[4]), .regdest(andi[6:5]), .re_wr(andi[7]), .alu_src(andi[8]),
    .mem_write(andi[9]), .mem_read(andi[10]), .mem_to_reg(andi[12:11]), .pc_next(andi[14:13]),
    .branch(andi[15]), .c_in(andi[16]), .shift_select(andi[18:17]));
  eqvi2 eqvi2_1 (
    .alu_op(eqvi[3:0]), .en(eqvi[4]), .regdest(eqvi[6:5]), .re_wr(eqvi[7]), .alu_src(eqvi[8]),
    .mem_write(eqvi[9]), .mem_read(eqvi[10]), .mem_to_reg(eqvi[12:11]), .pc_next(eqvi[14:13]),
    .branch(eqvi[15]), .c_in(eqvi[16]), .shift_select(eqvi[18:17]));
  ror2 ror2_1 (
    .alu_op(ror[3:0]), .en(ror[4]), .regdest(ror[6:5]), .re_wr(ror[7]), .alu_src(ror[8]), .mem_write(ror[9]),
    .mem_read(ror[10]), .mem_to_reg(ror[12:11]), .pc_next(ror[14:13]), .branch(ror[15]), .c_in(ror[16]),
    .shift_select(ror[18:17]));
  slti2 slti2_1 (
    .alu_op(slti[3:0]), .en(slti[4]), .regdest(slti[6:5]), .re_wr(slti[7]), .alu_src(slti[8]),
    .mem_write(slti[9]), .mem_read(slti[10]), .mem_to_reg(slti[12:11]), .pc_next(slti[14:13]),
    .branch(slti[15]), .c_in(slti[16]), .shift_select(slti[18:17]));
  ori2 ori2_1 (
    .alu_op(ori[3:0]), .en(ori[4]), .regdest(ori[6:5]), .re_wr(ori[7]), .alu_src(ori[8]), .mem_write(ori[9]),
    .mem_read(ori[10]), .mem_to_reg(ori[12:11]), .pc_next(ori[14:13]), .branch(ori[15]), .c_in(ori[16]),
    .shift_select(ori[18:17]));
  sll2 sll2_1 (
    .alu_op(sll[3:0]), .en(sll[4]), .regdest(sll[6:5]), .re_wr(sll[7]), .alu_src(sll[8]), .mem_write(sll[9]),
    .mem_read(sll[10]), .mem_to_reg(sll[12:11]), .pc_next(sll[14:13]), .branch(sll[15]), .c_in(sll[16]),
    .shift_select(sll[18:17]));
  seth2 seth2_1 (
    .alu_op(seth[3:0]), .en(seth[4]), .regdest(seth[6:5]), .re_wr(seth[7]), .alu_src(seth[8]),
    .mem_write(seth[9]), .mem_read(seth[10]), .mem_to_reg(seth[12:11]), .pc_next(seth[14:13]),
    .branch(seth[15]), .c_in(seth[16]), .shift_select(seth[18:17]));
  sltiu2 sltiu2_1 (
    .alu_op(sltiu[3:0]), .en(sltiu[4]), .regdest(sltiu[6:5]), .re_wr(sltiu[7]), .alu_src(sltiu[8]),
    .mem_write(sltiu[9]), .mem_read(sltiu[10]), .mem_to_reg(sltiu[12:11]), .pc_next(sltiu[14:13]),
    .branch(sltiu[15]), .c_in(sltiu[16]), .shift_select(sltiu[18:17]));
  xori2 xori2_1 (
    .alu_op(xori[3:0]), .en(xori[4]), .regdest(xori[6:5]), .re_wr(xori[7]), .alu_src(xori[8]),
    .mem_write(xori[9]), .mem_read(xori[10]), .mem_to_reg(xori[12:11]), .pc_next(xori[14:13]),
    .branch(xori[15]), .c_in(xori[16]), .shift_select(xori[18:17]));
  srl2 srl2_1 (
    .alu_op(srl[3:0]), .en(srl[4]), .regdest(srl[6:5]), .re_wr(srl[7]), .alu_src(srl[8]), .mem_write(srl[9]),
    .mem_read(srl[10]), .mem_to_reg(srl[12:11]), .pc_next(srl[14:13]), .branch(srl[15]), .c_in(srl[16]),
    .shift_select(srl[18:17]));
  ror2 ror2_2 (
    .alu_op(SRA[3:0]), .en(SRA[4]), .regdest(SRA[6:5]), .re_wr(SRA[7]), .alu_src(SRA[8]), .mem_write(SRA[9]),
    .mem_read(SRA[10]), .mem_to_reg(SRA[12:11]), .pc_next(SRA[14:13]), .branch(SRA[15]), .c_in(SRA[16]),
    .shift_select(SRA[18:17]));
  Multiplexer #(.select(4), .width(19)) multiplexer_1 (
    .in0(addi), .in1({19{1'b0}}), .in2(slti), .in3(sltiu), .in4(andi), .in5(ori), .in6(xori), .in7(eqvi),
    .in8(sll), .in9(srl), .in10(SRA), .in11(ror), .in12(seth), .in13({19{1'b0}}), .in14({19{1'b0}}),
    .in15({19{1'b0}}), .out(out_2), .sel(\input ));  // open: en
endmodule

module lw3 (
  output [3:0] alu_op,
  output en,
  output [1:0] regdest,
  output re_wr,
  output alu_src,
  output mem_write,
  output mem_read,
  output [1:0] mem_to_reg,
  output [1:0] pc_next,
  output branch,
  output c_in,
  output [1:0] shift_select
);


  assign alu_op = 4'b0011;
  assign alu_src = 1'b1;
  assign branch = 1'b0;
  assign c_in = 1'b0;
  assign en = 1'b1;
  assign mem_read = 1'b1;
  assign mem_to_reg = 2'b01;
  assign mem_write = 1'b0;
  assign pc_next = 2'b00;
  assign re_wr = 1'b1;
  assign regdest = 2'b00;
  assign shift_select = 2'b00;
endmodule

module sw3 (
  output [3:0] alu_op,
  output en,
  output [1:0] regdest,
  output re_wr,
  output alu_src,
  output mem_write,
  output mem_read,
  output [1:0] mem_to_reg,
  output [1:0] pc_next,
  output branch,
  output c_in,
  output [1:0] shift_select
);


  assign alu_op = 4'b0011;
  assign alu_src = 1'b1;
  assign branch = 1'b0;
  assign c_in = 1'b0;
  assign en = 1'b1;
  assign mem_read = 1'b0;
  assign mem_to_reg = 2'b00;
  assign mem_write = 1'b1;
  assign pc_next = 2'b00;
  assign re_wr = 1'b0;
  assign regdest = 2'b00;
  assign shift_select = 2'b00;
endmodule

module type_3 (
  input  [3:0] \input ,
  output [18:0] out_2
);

  wire [18:0] lw, sw;

  lw3 lw3_1 (
    .alu_op(lw[3:0]), .en(lw[4]), .regdest(lw[6:5]), .re_wr(lw[7]), .alu_src(lw[8]), .mem_write(lw[9]),
    .mem_read(lw[10]), .mem_to_reg(lw[12:11]), .pc_next(lw[14:13]), .branch(lw[15]), .c_in(lw[16]),
    .shift_select(lw[18:17]));
  sw3 sw3_1 (
    .alu_op(sw[3:0]), .en(sw[4]), .regdest(sw[6:5]), .re_wr(sw[7]), .alu_src(sw[8]), .mem_write(sw[9]),
    .mem_read(sw[10]), .mem_to_reg(sw[12:11]), .pc_next(sw[14:13]), .branch(sw[15]), .c_in(sw[16]),
    .shift_select(sw[18:17]));
  Multiplexer #(.select(4), .width(19)) multiplexer_1 (
    .in0(lw), .in1(sw), .in2({19{1'b0}}), .in3({19{1'b0}}), .in4({19{1'b0}}), .in5({19{1'b0}}),
    .in6({19{1'b0}}), .in7({19{1'b0}}), .in8({19{1'b0}}), .in9({19{1'b0}}), .in10({19{1'b0}}),
    .in11({19{1'b0}}), .in12({19{1'b0}}), .in13({19{1'b0}}), .in14({19{1'b0}}), .in15({19{1'b0}}),
    .out(out_2), .sel(\input ));  // open: en
endmodule

module beq4 (
  output [3:0] alu_op,
  output en,
  output [1:0] regdest,
  output re_wr,
  output alu_src,
  output mem_write,
  output mem_read,
  output [1:0] mem_to_reg,
  output [1:0] pc_next,
  output branch,
  output c_in,
  output [1:0] shift_select
);


  assign alu_op = 4'b0000;
  assign alu_src = 1'b1;
  assign branch = 1'b1;
  assign c_in = 1'b0;
  assign en = 1'b1;
  assign mem_read = 1'b0;
  assign mem_to_reg = 2'b00;
  assign mem_write = 1'b0;
  assign pc_next = 2'b00;
  assign re_wr = 1'b0;
  assign regdest = 2'b11;
  assign shift_select = 2'b00;
endmodule

module benq4 (
  output [3:0] alu_op,
  output en,
  output [1:0] regdest,
  output re_wr,
  output alu_src,
  output mem_write,
  output mem_read,
  output [1:0] mem_to_reg,
  output [1:0] pc_next,
  output branch,
  output c_in,
  output [1:0] shift_select
);


  assign alu_op = 4'b0000;
  assign alu_src = 1'b1;
  assign branch = 1'b1;
  assign c_in = 1'b0;
  assign en = 1'b1;
  assign mem_read = 1'b0;
  assign mem_to_reg = 2'b00;
  assign mem_write = 1'b0;
  assign pc_next = 2'b11;
  assign re_wr = 1'b0;
  assign regdest = 2'b11;
  assign shift_select = 2'b00;
endmodule

module type_4 (
  input  [3:0] \input ,
  output [18:0] out_2
);

  wire [18:0] benq, beq;

  beq4 beq4_1 (
    .alu_op(beq[3:0]), .en(beq[4]), .regdest(beq[6:5]), .re_wr(beq[7]), .alu_src(beq[8]), .mem_write(beq[9]),
    .mem_read(beq[10]), .mem_to_reg(beq[12:11]), .pc_next(beq[14:13]), .branch(beq[15]), .c_in(beq[16]),
    .shift_select(beq[18:17]));
  benq4 benq4_1 (
    .alu_op(benq[3:0]), .en(benq[4]), .regdest(benq[6:5]), .re_wr(benq[7]), .alu_src(benq[8]),
    .mem_write(benq[9]), .mem_read(benq[10]), .mem_to_reg(benq[12:11]), .pc_next(benq[14:13]),
    .branch(benq[15]), .c_in(benq[16]), .shift_select(benq[18:17]));
  Multiplexer #(.select(4), .width(19)) multiplexer_1 (
    .in0(beq), .in1(benq), .in2({19{1'b0}}), .in3({19{1'b0}}), .in4({19{1'b0}}), .in5({19{1'b0}}),
    .in6({19{1'b0}}), .in7({19{1'b0}}), .in8({19{1'b0}}), .in9({19{1'b0}}), .in10({19{1'b0}}),
    .in11({19{1'b0}}), .in12({19{1'b0}}), .in13({19{1'b0}}), .in14({19{1'b0}}), .in15({19{1'b0}}),
    .out(out_2), .sel(\input ));  // open: en
endmodule

module jr5 (
  output [3:0] alu_op,
  output en,
  output [1:0] regdest,
  output re_wr,
  output alu_src,
  output mem_write,
  output mem_read,
  output [1:0] mem_to_reg,
  output [1:0] pc_next,
  output branch,
  output c_in,
  output [1:0] shift_select
);


  assign alu_op = 4'b0000;
  assign alu_src = 1'b1;
  assign branch = 1'b0;
  assign c_in = 1'b0;
  assign en = 1'b1;
  assign mem_read = 1'b0;
  assign mem_to_reg = 2'b00;
  assign mem_write = 1'b0;
  assign pc_next = 2'b10;
  assign re_wr = 1'b0;
  assign regdest = 2'b11;
  assign shift_select = 2'b00;
endmodule

module jalr5 (
  output [3:0] alu_op,
  output en,
  output [1:0] regdest,
  output re_wr,
  output alu_src,
  output mem_write,
  output mem_read,
  output [1:0] mem_to_reg,
  output [1:0] pc_next,
  output branch,
  output c_in,
  output [1:0] shift_select
);


  assign alu_op = 4'b0000;
  assign alu_src = 1'b1;
  assign branch = 1'b0;
  assign c_in = 1'b0;
  assign en = 1'b1;
  assign mem_read = 1'b0;
  assign mem_to_reg = 2'b10;
  assign mem_write = 1'b0;
  assign pc_next = 2'b10;
  assign re_wr = 1'b1;
  assign regdest = 2'b00;
  assign shift_select = 2'b00;
endmodule

module type_5 (
  input  [3:0] \input ,
  output [18:0] out_2
);

  wire [18:0] jalr, jr;

  jr5 jr5_1 (
    .alu_op(jr[3:0]), .en(jr[4]), .regdest(jr[6:5]), .re_wr(jr[7]), .alu_src(jr[8]), .mem_write(jr[9]),
    .mem_read(jr[10]), .mem_to_reg(jr[12:11]), .pc_next(jr[14:13]), .branch(jr[15]), .c_in(jr[16]),
    .shift_select(jr[18:17]));
  jalr5 jalr5_1 (
    .alu_op(jalr[3:0]), .en(jalr[4]), .regdest(jalr[6:5]), .re_wr(jalr[7]), .alu_src(jalr[8]),
    .mem_write(jalr[9]), .mem_read(jalr[10]), .mem_to_reg(jalr[12:11]), .pc_next(jalr[14:13]),
    .branch(jalr[15]), .c_in(jalr[16]), .shift_select(jalr[18:17]));
  Multiplexer #(.select(4), .width(19)) multiplexer_1 (
    .in0(jr), .in1(jalr), .in2({19{1'b0}}), .in3({19{1'b0}}), .in4({19{1'b0}}), .in5({19{1'b0}}),
    .in6({19{1'b0}}), .in7({19{1'b0}}), .in8({19{1'b0}}), .in9({19{1'b0}}), .in10({19{1'b0}}),
    .in11({19{1'b0}}), .in12({19{1'b0}}), .in13({19{1'b0}}), .in14({19{1'b0}}), .in15({19{1'b0}}),
    .out(out_2), .sel(\input ));  // open: en
endmodule

module j_6 (
  output [3:0] alu_op,
  output en,
  output [1:0] regdest,
  output re_wr,
  output alu_src,
  output mem_write,
  output mem_read,
  output [1:0] mem_to_reg,
  output [1:0] pc_next,
  output branch,
  output c_in,
  output [1:0] shift_select
);


  assign alu_op = 4'b0000;
  assign alu_src = 1'b1;
  assign branch = 1'b0;
  assign c_in = 1'b0;
  assign en = 1'b1;
  assign mem_read = 1'b0;
  assign mem_to_reg = 2'b00;
  assign mem_write = 1'b0;
  assign pc_next = 2'b01;
  assign re_wr = 1'b0;
  assign regdest = 2'b11;
  assign shift_select = 2'b00;
endmodule

module jal_6 (
  output [3:0] alu_op,
  output en,
  output [1:0] regdest,
  output re_wr,
  output alu_src,
  output mem_write,
  output mem_read,
  output [1:0] mem_to_reg,
  output [1:0] pc_next,
  output branch,
  output c_in,
  output [1:0] shift_select
);


  assign alu_op = 4'b0000;
  assign alu_src = 1'b1;
  assign branch = 1'b0;
  assign c_in = 1'b0;
  assign en = 1'b1;
  assign mem_read = 1'b0;
  assign mem_to_reg = 2'b10;
  assign mem_write = 1'b0;
  assign pc_next = 2'b01;
  assign re_wr = 1'b1;
  assign regdest = 2'b10;
  assign shift_select = 2'b00;
endmodule

module type_6 (
  input  [3:0] \input ,
  output [18:0] out_2
);

  wire [18:0] j, jal;

  j_6 j_6_1 (
    .alu_op(j[3:0]), .en(j[4]), .regdest(j[6:5]), .re_wr(j[7]), .alu_src(j[8]), .mem_write(j[9]),
    .mem_read(j[10]), .mem_to_reg(j[12:11]), .pc_next(j[14:13]), .branch(j[15]), .c_in(j[16]),
    .shift_select(j[18:17]));
  jal_6 jal_6_1 (
    .alu_op(jal[3:0]), .en(jal[4]), .regdest(jal[6:5]), .re_wr(jal[7]), .alu_src(jal[8]), .mem_write(jal[9]),
    .mem_read(jal[10]), .mem_to_reg(jal[12:11]), .pc_next(jal[14:13]), .branch(jal[15]), .c_in(jal[16]),
    .shift_select(jal[18:17]));
  Multiplexer #(.select(4), .width(19)) multiplexer_1 (
    .in0(j), .in1(jal), .in2({19{1'b0}}), .in3({19{1'b0}}), .in4({19{1'b0}}), .in5({19{1'b0}}),
    .in6({19{1'b0}}), .in7({19{1'b0}}), .in8({19{1'b0}}), .in9({19{1'b0}}), .in10({19{1'b0}}),
    .in11({19{1'b0}}), .in12({19{1'b0}}), .in13({19{1'b0}}), .in14({19{1'b0}}), .in15({19{1'b0}}),
    .out(out_2), .sel(\input ));  // open: en
endmodule

module exit_6 (
  output [3:0] alu_op,
  output en,
  output [1:0] regdest,
  output re_wr,
  output alu_src,
  output mem_write,
  output mem_read,
  output [1:0] mem_to_reg,
  output [1:0] pc_next,
  output branch,
  output c_in,
  output [1:0] shift_select
);


  assign alu_op = 4'b0010;
  assign alu_src = 1'b0;
  assign branch = 1'b0;
  assign c_in = 1'b0;
  assign en = 1'b0;
  assign mem_read = 1'b0;
  assign mem_to_reg = 2'b00;
  assign mem_write = 1'b0;
  assign pc_next = 2'b00;
  assign re_wr = 1'b1;
  assign regdest = 2'b01;
  assign shift_select = 2'b00;
endmodule
